# Fritzing sketch hardware-design (saved by Fritzing 0.9.3b)

parts:
  Raspberry_Pi_1 = Raspberry Pi 4 [part_number=RPI-4-b]
  PWM1 = PCA9685 16x12-bit PWM Breakout
  SERVO1 = Tower Pro SG90 servo [part_number=101246]
  USBTTL1 = USB A Plug  # not connected
  BAT1 = 6v battery [package=battery]
  SERVO2 = Tower Pro SG90 servo [part_number=101246]
  SERVO3 = Tower Pro SG90 servo [part_number=101246]
  SERVO4 = Tower Pro SG90 servo [part_number=101246]
  SERVO5 = Tower Pro SG90 servo [part_number=101246]
  USBTTL2 = USB A Plug  # not connected
  Power_plug1 = USB-C plug
  Power_plug2 = USB-C plug

nets:
  N1: Raspberry_Pi_1.3v3, PWM1.no_name_yet#505
  N2: Raspberry_Pi_1.GPIO2, PWM1.no_name_yet#504
  N3: Raspberry_Pi_1.GPIO3, PWM1.no_name_yet#503
  GND: Raspberry_Pi_1.GND, PWM1.no_name_yet#501, PWM1.no_name_yet#701, PWM1.no_name_yet#1000, PWM1.no_name_yet#1001, PWM1.no_name_yet#1002, PWM1.no_name_yet#1003, PWM1.no_name_yet#1004, SERVO1.GND, BAT1.-, SERVO2.GND, SERVO3.GND, SERVO4.GND, SERVO5.GND
  N4: PWM1.no_name_yet#0, SERVO1.Signal
  N5: PWM1.no_name_yet#1, SERVO2.Signal
  N6: PWM1.no_name_yet#2, SERVO3.Signal
  N7: PWM1.no_name_yet#3, SERVO4.Signal
  N8: PWM1.no_name_yet#4, SERVO5.Signal
  +5V: PWM1.no_name_yet#100, PWM1.no_name_yet#101, PWM1.no_name_yet#102, PWM1.no_name_yet#103, PWM1.no_name_yet#104, PWM1.no_name_yet#706, SERVO1.+5V, BAT1.+, SERVO2.+5V, SERVO3.+5V, SERVO4.+5V, SERVO5.+5V
  GND_2: Power_plug1.GND, Power_plug2.GND
  VCC: Power_plug1.VCC, Power_plug2.VCC

notes:
  ⁨USB Microphone
  USB Camara
  Bluetooth speaker
  Portable charger

custom parts:
  Raspberry Pi 4: The RPi4, a faster version of the awesome Raspberry Pi 2 B ARM Board with 40 pin gpio. Ready for special Raspberry Pi B+ and RPi2 Hat (Hardware attached (on) top)
  Tower Pro SG90 servo: Original file by John De Cristofaro http://www.adafruit.com/products/1449 Adafruit Feedback Servo (Small) Edited by: e-radionica.com 28/9/2015
  USB A Plug: USB A Plug breadboard only for documetnation purposes.
  6v battery: 6V lead acid battery 12ah
  USB-C plug: power plug
